// Logisim project control-logic.circ as structural Verilog: 1 circuit, main circuit control_logic
module control_logic (
  input  [31:0] Instruction,
  input  BrEq,
  input  BrLt,
  output PCSel,
  output RegWEn,
  output [2:0] ImmSel,
  output BrUn,
  output ASel,
  output BSel,
  output [3:0] ALUSel,
  output MemWEn,
  output [1:0] WBSel
);

  wire and_9_out, and_10_out, and_11_out, and_12_out, and_13_out, and_14_out, comparator_2_eq,
       comparator_3_eq, comparator_4_eq, comparator_5_eq, comparator_6_eq, comparator_7_eq, comparator_8_eq,
       comparator_9_eq, comparator_10_eq, comparator_11_eq, comparator_12_eq, comparator_13_eq,
       comparator_14_eq, comparator_15_eq, comparator_16_eq, comparator_17_eq, comparator_18_eq,
       comparator_19_eq, comparator_20_eq, comparator_21_eq, comparator_22_eq, comparator_23_eq,
       comparator_25_eq, comparator_26_eq, comparator_27_eq, comparator_28_eq, comparator_29_eq,
       comparator_30_eq, comparator_31_eq, comparator_32_eq, comparator_33_eq, comparator_34_eq,
       comparator_35_eq, comparator_36_eq, comparator_37_eq, comparator_38_eq, isAdd, isAddi, isAnd, isAndi,
       isBeq, isBge, isBgeu, isBlt, isBltu, isBne, isBType, isIType, isMul, isMulh, isMulhu, isOr, isOri,
       isRType, isSll, isSlli, isSlt, isSlti, isSra, isSrai, isSrl, isSrli, isSub, isXor, isXori, not_1_out,
       not_2_out, not_3_out, or_1_out;
  wire [5:0] ROMIn;
  wire [15:14] rom_1_data;

  ROM #(.addrWidth(6), .dataWidth(16)) rom_1 (
    .addr(ROMIn), .data({rom_1_data, WBSel, MemWEn, ALUSel, BSel, ASel, BrUn, ImmSel, RegWEn}));
  Priority_Encoder #(.select_enc(6)) priority_encoder_1 (
    .in3(isAddi), .in4(isSlli), .in5(isSlti), .in6(isXori), .in7(isSrli), .in8(isSrai), .in9(isOri),
    .in10(isAndi), .in11(isAdd), .in12(isMul), .in13(isSub), .in14(isSll), .in15(isMulh), .in16(isMulhu),
    .in17(isSlt), .in18(isXor), .in19(isSrl), .in20(isSra), .in21(isOr), .in22(isAnd), .in23(isBeq),
    .in24(isBne), .in25(isBlt), .in26(isBge), .in27(isBltu), .in28(isBgeu), .out(ROMIn));  // open: in0, in1, in2, in29, in30, in31, in32, in33, in34, in35, in36, in37, in38, in39, in40, in41, in42, in43, in44, in45, in46, in47, in48, in49, in50, in51, in52, in53, in54, in55, in56, in57, in58, in59, in60, in61, in62, in63, gs, en_out, en_in
  Comparator #(.width(7)) comparator_1 (.a(Instruction[6:0]), .b(7'b0010011), .eq(isIType));  // open: gt, lt
  Comparator #(.width(3)) comparator_2 (.a(Instruction[14:12]), .b(3'b000), .eq(comparator_2_eq));  // open: gt, lt
  Comparator #(.width(3)) comparator_3 (.a(Instruction[14:12]), .b(3'b001), .eq(comparator_3_eq));  // open: gt, lt
  Comparator #(.width(3)) comparator_4 (.a(Instruction[14:12]), .b(3'b101), .eq(comparator_4_eq));  // open: gt, lt
  Comparator #(.width(7)) comparator_5 (.a(Instruction[31:25]), .b(7'b0100000), .eq(comparator_5_eq));  // open: gt, lt
  Comparator #(.width(3)) comparator_6 (.a(Instruction[14:12]), .b(3'b101), .eq(comparator_6_eq));  // open: gt, lt
  Comparator #(.width(3)) comparator_7 (.a(Instruction[14:12]), .b(3'b111), .eq(comparator_7_eq));  // open: gt, lt
  Comparator #(.width(3)) comparator_8 (.a(Instruction[14:12]), .b(3'b110), .eq(comparator_8_eq));  // open: gt, lt
  Comparator #(.width(3)) comparator_9 (.a(Instruction[14:12]), .b(3'b010), .eq(comparator_9_eq));  // open: gt, lt
  Comparator #(.width(3)) comparator_10 (.a(Instruction[14:12]), .b(3'b100), .eq(comparator_10_eq));  // open: gt, lt
  Comparator #(.width(7)) comparator_11 (.a(Instruction[31:25]), .b({7{1'b0}}), .eq(comparator_11_eq));  // open: gt, lt
  and and_1 (isAddi, isIType, comparator_2_eq);
  and and_2 (isSlli, isIType, comparator_3_eq);
  and and_3 (isSlti, isIType, comparator_9_eq);
  and and_4 (isXori, isIType, comparator_10_eq);
  and and_5 (isSrli, isIType, comparator_11_eq, comparator_4_eq);
  and and_6 (isSrai, isIType, comparator_5_eq, comparator_6_eq);
  and and_7 (isAndi, isIType, comparator_7_eq);
  and and_8 (isOri, isIType, comparator_8_eq);
  not not_1 (not_1_out, BrEq);
  not not_2 (not_2_out, BrLt);
  not not_3 (not_3_out, BrLt);
  and and_9 (and_9_out, BrEq, isBeq);
  and and_10 (and_10_out, not_1_out, isBne);
  and and_11 (and_11_out, BrLt, isBlt);
  and and_12 (and_12_out, not_2_out, isBge);
  and and_13 (and_13_out, BrLt, isBltu);
  and and_14 (and_14_out, not_3_out, isBgeu);
  or or_1 (or_1_out, and_9_out, and_10_out, and_11_out, and_12_out, and_13_out, and_14_out);
  Comparator #(.width(3)) comparator_12 (.a(Instruction[14:12]), .b(3'b001), .eq(comparator_12_eq));  // open: gt, lt
  Comparator #(.width(3)) comparator_13 (.a(Instruction[14:12]), .b(3'b001), .eq(comparator_13_eq));  // open: gt, lt
  Comparator #(.width(7)) comparator_14 (
    .a(Instruction[31:25]), .b(7'b0000001), .eq(comparator_14_eq));  // open: gt, lt
  Comparator #(.width(3)) comparator_15 (.a(Instruction[14:12]), .b(3'b011), .eq(comparator_15_eq));  // open: gt, lt
  Comparator #(.width(3)) comparator_16 (.a(Instruction[14:12]), .b(3'b010), .eq(comparator_16_eq));  // open: gt, lt
  Comparator #(.width(3)) comparator_17 (.a(Instruction[14:12]), .b(3'b100), .eq(comparator_17_eq));  // open: gt, lt
  Comparator #(.width(7)) comparator_18 (.a(Instruction[31:25]), .b({7{1'b0}}), .eq(comparator_18_eq));  // open: gt, lt
  Comparator #(.width(3)) comparator_19 (.a(Instruction[14:12]), .b(3'b101), .eq(comparator_19_eq));  // open: gt, lt
  Comparator #(.width(7)) comparator_20 (
    .a(Instruction[31:25]), .b(7'b0100000), .eq(comparator_20_eq));  // open: gt, lt
  Comparator #(.width(3)) comparator_21 (.a(Instruction[14:12]), .b(3'b101), .eq(comparator_21_eq));  // open: gt, lt
  Comparator #(.width(3)) comparator_22 (.a(Instruction[14:12]), .b(3'b110), .eq(comparator_22_eq));  // open: gt, lt
  Comparator #(.width(3)) comparator_23 (.a(Instruction[14:12]), .b(3'b111), .eq(comparator_23_eq));  // open: gt, lt
  Comparator #(.width(7)) comparator_24 (.a(Instruction[6:0]), .b(7'b0110011), .eq(isRType));  // open: gt, lt
  Comparator #(.width(7)) comparator_25 (.a(Instruction[31:25]), .b({7{1'b0}}), .eq(comparator_25_eq));  // open: gt, lt
  Comparator #(.width(3)) comparator_26 (.a(Instruction[14:12]), .b(3'b000), .eq(comparator_26_eq));  // open: gt, lt
  Comparator #(.width(7)) comparator_27 (
    .a(Instruction[31:25]), .b(7'b0000001), .eq(comparator_27_eq));  // open: gt, lt
  Comparator #(.width(3)) comparator_28 (.a(Instruction[14:12]), .b(3'b000), .eq(comparator_28_eq));  // open: gt, lt
  Comparator #(.width(7)) comparator_29 (
    .a(Instruction[31:25]), .b(7'b0100000), .eq(comparator_29_eq));  // open: gt, lt
  Comparator #(.width(3)) comparator_30 (.a(Instruction[14:12]), .b(3'b000), .eq(comparator_30_eq));  // open: gt, lt
  Comparator #(.width(7)) comparator_31 (.a(Instruction[31:25]), .b({7{1'b0}}), .eq(comparator_31_eq));  // open: gt, lt
  Comparator #(.width(7)) comparator_32 (
    .a(Instruction[31:25]), .b(7'b0000001), .eq(comparator_32_eq));  // open: gt, lt
  and and_15 (isXor, isRType, comparator_17_eq);
  and and_16 (isSrl, isRType, comparator_18_eq, comparator_19_eq);
  and and_17 (isSra, isRType, comparator_20_eq, comparator_21_eq);
  and and_18 (isOr, isRType, comparator_22_eq);
  and and_19 (isAnd, isRType, comparator_23_eq);
  and and_20 (PCSel, isBType, or_1_out);
  and and_21 (isAdd, isRType, comparator_25_eq, comparator_26_eq);
  and and_22 (isMul, isRType, comparator_27_eq, comparator_28_eq);
  and and_23 (isSub, isRType, comparator_29_eq, comparator_30_eq);
  and and_24 (isSll, isRType, comparator_31_eq, comparator_12_eq);
  and and_25 (isMulh, isRType, comparator_32_eq, comparator_13_eq);
  and and_26 (isMulhu, isRType, comparator_14_eq, comparator_15_eq);
  and and_27 (isSlt, isRType, comparator_16_eq);
  Comparator #(.width(3)) comparator_33 (.a(Instruction[14:12]), .b(3'b000), .eq(comparator_33_eq));  // open: gt, lt
  Comparator #(.width(3)) comparator_34 (.a(Instruction[14:12]), .b(3'b001), .eq(comparator_34_eq));  // open: gt, lt
  Comparator #(.width(3)) comparator_35 (.a(Instruction[14:12]), .b(3'b100), .eq(comparator_35_eq));  // open: gt, lt
  Comparator #(.width(3)) comparator_36 (.a(Instruction[14:12]), .b(3'b101), .eq(comparator_36_eq));  // open: gt, lt
  Comparator #(.width(3)) comparator_37 (.a(Instruction[14:12]), .b(3'b110), .eq(comparator_37_eq));  // open: gt, lt
  Comparator #(.width(3)) comparator_38 (.a(Instruction[14:12]), .b(3'b111), .eq(comparator_38_eq));  // open: gt, lt
  Comparator #(.width(7)) comparator_39 (.a(Instruction[6:0]), .b(7'b1100011), .eq(isBType));  // open: gt, lt
  and and_28 (isBeq, isBType, comparator_33_eq);
  and and_29 (isBne, isBType, comparator_34_eq);
  and and_30 (isBlt, isBType, comparator_35_eq);
  and and_31 (isBge, isBType, comparator_36_eq);
  and and_32 (isBltu, isBType, comparator_37_eq);
  and and_33 (isBgeu, isBType, comparator_38_eq);

  // Other names for the same wires on the sheet: opcode[6:0] = Instruction[6:0]; rd[4:0] = Instruction[11:7];
  //   funct3[2:0] = Instruction[14:12]; rs1[4:0] = Instruction[19:15]; funct7[6:0] = Instruction[31:25]

  // Notes on the sheet:
  //   INPUTS to your circuit
  //   Connect ROM Input here ->
  //   contents of rom_1 (hex, n*v repeats v):
  //   41 41 41 1041 10c1 1141 1241 12c1 16c1 1341 13c1 1 401 601 81 481 581 101 201 281 681 301 381 4*64
  //   74 74 74
  //   ROM FOR CONTROL LOGIC
  //   DON'T CHANGE THE LOCATIONS OF THE INPUTS AND OUTPUTS!
  //   This is only if you choose to do the ROM option
  //   CONNECT
  //   WIRE
  //   TO
  //   USE
  //   ROM
  //   OUTPUT from your circuit
  //   I-Type
  //   Reminder: If using ROM, use combinational logic for PCSel
  //   R-Type
  //   B-Type
endmodule
