// Logisim project partial-store.circ as structural Verilog: 1 circuit, main circuit partial_store
module partial_store (
  input  [31:0] Instruction,
  input  [31:0] MemAddress,
  input  [31:0] DataFromReg,
  input  MemWEn,
  output [3:0] MemWriteMask,
  output [31:0] DataToMem
);

  wire comparator_2_eq, comparator_3_eq, comparator_4_eq, comparator_5_eq, comparator_6_eq, comparator_7_eq,
       comparator_8_eq, comparator_9_eq, comparator_10_eq, comparator_11_eq, isSb, isSb0, isSb1, isSb2,
       isSb3, isSh, isSh0, isSh1, isStore, isSw, isSwOut;
  wire [2:0] maskSel;
  wire [31:0] multiplexer_1_out;

  Comparator #(.width(7)) comparator_1 (.a(Instruction[6:0]), .b(7'b0100011), .eq(isStore));  // open: gt, lt
  Comparator #(.width(3)) comparator_2 (.a(Instruction[14:12]), .b(3'b000), .eq(comparator_2_eq));  // open: gt, lt
  Comparator #(.width(3)) comparator_3 (.a(Instruction[14:12]), .b(3'b001), .eq(comparator_3_eq));  // open: gt, lt
  Comparator #(.width(3)) comparator_4 (.a(Instruction[14:12]), .b(3'b010), .eq(comparator_4_eq));  // open: gt, lt
  and and_1 (isSb, isStore, comparator_2_eq);
  and and_2 (isSh, isStore, comparator_3_eq);
  and and_3 (isSw, isStore, comparator_4_eq);
  Comparator #(.width(2)) comparator_5 (.a(MemAddress[1:0]), .b(2'b00), .eq(comparator_5_eq));  // open: gt, lt
  Comparator #(.width(2)) comparator_6 (.a(MemAddress[1:0]), .b(2'b01), .eq(comparator_6_eq));  // open: gt, lt
  Comparator #(.width(2)) comparator_7 (.a(MemAddress[1:0]), .b(2'b10), .eq(comparator_7_eq));  // open: gt, lt
  Comparator #(.width(2)) comparator_8 (.a(MemAddress[1:0]), .b(2'b11), .eq(comparator_8_eq));  // open: gt, lt
  Comparator #(.width(2)) comparator_9 (.a(MemAddress[1:0]), .b(2'b00), .eq(comparator_9_eq));  // open: gt, lt
  Comparator #(.width(2)) comparator_10 (.a(MemAddress[1:0]), .b(2'b01), .eq(comparator_10_eq));  // open: gt, lt
  Comparator #(.width(2)) comparator_11 (.a(MemAddress[1:0]), .b(2'b00), .eq(comparator_11_eq));  // open: gt, lt
  and and_4 (isSb0, isSb, comparator_5_eq);
  and and_5 (isSb1, isSb, comparator_6_eq);
  and and_6 (isSb2, isSb, comparator_7_eq);
  and and_7 (isSb3, isSb, comparator_8_eq);
  and and_8 (isSh0, isSh, comparator_9_eq);
  and and_9 (isSh1, isSh, comparator_10_eq);
  and and_10 (isSwOut, isSw, comparator_11_eq);
  Multiplexer #(.select(3), .width(32)) multiplexer_1 (
    .in0(32'hff), .in1(32'hff00), .in2(32'hff0000), .in3(32'hff000000), .in4(32'hffff), .in5(32'hffff0000),
    .out(multiplexer_1_out), .sel(maskSel));  // open: in6, in7
  Priority_Encoder priority_encoder_1 (
    .in0(isSb0), .in1(isSb1), .in2(isSb2), .in3(isSb3), .in4(isSh0), .in5(isSh1), .out(maskSel));  // open: in6, in7, en_in, gs, en_out
  assign DataToMem = DataFromReg & multiplexer_1_out;  // AND_Gate and_11, 32 bits wide
  Multiplexer #(.select(3), .width(4)) multiplexer_2 (
    .in0(4'b0001), .in1(4'b0010), .in2(4'b0100), .in3(4'b1000), .in4(4'b0011), .in5(4'b1100), .in6(4'b1111),
    .out(MemWriteMask), .sel(maskSel));  // open: in7

  // Other names for the same wires on the sheet: opcode[6:0] = Instruction[6:0]; funct3[2:0] = Instruction[14:12];
  //   bottom2bits[1:0] = MemAddress[1:0]

  // Notes on the sheet:
  //   INPUTS to your circuit
  //   DON'T CHANGE THE LOCATIONS OF THE INPUTS AND OUTPUTS!
  //   OUTPUT from your circuit
endmodule
